// Logisim project Conexion al motor.circ as structural Verilog: 1 circuit, main circuit main
module main (
  input  Abrir_Cerrar,
  input  Fuente_del_motor,
  output Corriente_al_motor
);

  Transistor #(.\type ("n")) transistor_1 (.in(Fuente_del_motor), .out(Corriente_al_motor), .gate(Abrir_Cerrar));

  // Notes on the sheet:
  //   Logisim no cuenta con transistor bipolar, entonces de manera simbolica se usa un transistor de efecto de campo
  //   Conexión a el motor
endmodule
