// Logisim project Logic_Simulation.circ as structural Verilog: 1 circuit, main circuit main
module main (
  input  A0,
  input  A1,
  input  P,
  input  A2,
  input  A0_2,
  input  A1_2,
  input  A2_2,
  input  S1,
  input  A0_3,
  input  A1_3,
  input  A2_3,
  output Eq1,
  output S0,
  output C,
  output Eq2,
  output LED_Verde,
  output Eq3,
  output LED_Rojo
);

  wire and_5_out, not_1_out, not_2_out, not_3_out, not_4_out, not_5_out, not_6_out;

  not not_1 (not_1_out, A1);
  not not_2 (not_2_out, A2);
  not not_3 (not_3_out, A0_2);
  not not_4 (not_4_out, A1_2);
  not not_5 (not_5_out, A2_3);
  and and_1 (Eq1, A0, not_1_out, not_2_out);
  and and_2 (Eq2, not_3_out, not_4_out, A2_2);
  and and_3 (Eq3, A0_3, A1_3, not_5_out);
  and and_4 (C, Eq1, Eq2, Eq3);
  and and_5 (and_5_out, P, C);
  not not_6 (not_6_out, C);
  D_Flip_Flop d_ff_1 (.clk(and_5_out), .D(LED_Rojo), .Q(LED_Verde), .Qn(LED_Rojo));  // open: preset, en, reset
  and and_6 (S0, P, not_6_out);
endmodule
