// Logisim project Mecanismo de cerrado.circ as structural Verilog: 1 circuit, main circuit main
module main (
  input  Correcto,
  input  Confirmar,
  output Abrir_Cerrar
);

  wire and_1_out, and_2_out, and_3_out, clock_1_out, d_ff_1_q, not_1_out;

  D_Flip_Flop d_ff_1 (.clk(clock_1_out), .D(Correcto), .Q(d_ff_1_q));  // open: Qn, preset, en, reset
  not not_1 (not_1_out, d_ff_1_q);
  Clock clock_1 (.out(clock_1_out));
  and and_1 (and_1_out, not_1_out, Confirmar);
  and and_2 (and_2_out, Correcto, Confirmar);
  T_Flip_Flop t_ff_1 (.clk(clock_1_out), .T(and_3_out), .Q(Abrir_Cerrar));  // open: Qn, preset, reset, en
  and and_3 (and_3_out, and_1_out, and_2_out);

  // Notes on the sheet:
  //   Confirmar es un botón
  //   Mecanismo de cerrado
endmodule
